# Fritzing sketch Bday_Card (saved by Fritzing 0.7.12b)
breadboards: 1

parts:
  Crystal = Crystal [frequency="16 Mhz" package=THT]
  Ceramic = Ceramic Capacitor [capacitance=100nF package="100 mil [THT, multilayer]"]
  Capacitors = Ceramic Capacitor [capacitance=100nF package="100 mil [THT, multilayer]"]
  Regulator = Voltage Regulator - 5V [package="TO220 [THT]"]
  C8 = Electrolytic Capacitor [capacitance=10µF package="100 mil [THT, electrolytic]"]
  Capacitor = Electrolytic Capacitor [capacitance=10µF package="100 mil [THT, electrolytic]"]
  ATMega328 = atmega328 [part_number=ATMega328 package=dip]
  + = female pin header, 1 pin [form="♀ (female)"]
  - = female pin header, 1 pin [form="♀ (female)"]
  Speaker_- = female pin header, 1 pin [form="♀ (female)"]
  Spkr_+ = female pin header, 1 pin [form="♀ (female)"]
  Resistors = Resistor [tolerance=±5% resistance=4.7k package=THT]
  4_7_kΩ = Resistor [tolerance=±5% resistance=4.7k package=THT]
  R1 = Resistor [tolerance=±5% resistance=4.7k package=THT]
  Button = Pushbutton [package="[THT]"]
  220Ω_Resistor = Resistor [tolerance=±5% resistance=220 package=THT]

nets:
  N1: Crystal.pin_0, Capacitors.1, ATMega328.XLAT1
  N2: Crystal.pin_1, Ceramic.1, ATMega328.XLAT2
  GND: Ceramic.0, Capacitors.0, Regulator.GND, C8.-, Capacitor.-, ATMega328.GND, -.pin1, Speaker_-.pin1, 220Ω_Resistor.Pin_0
  N3: Regulator.input_voltage, Capacitor.+, +.pin1
  N4: Regulator.output_voltage, C8.+, ATMega328.VCC, ATMega328.AVCC, ATMega328.AREF, Button.Pin_1, Button.Pin_2
  N5: ATMega328.D5_(PWM), R1.Pin_0
  N6: ATMega328.D6_(PWM), Resistors.Pin_0
  N7: ATMega328.D9_(PWM), 4_7_kΩ.Pin_0
  N8: ATMega328.D10_(PWM), Button.Pin_3, Button.Pin_4, 220Ω_Resistor.Pin_1
  N9: Spkr_+.pin1, Resistors.Pin_1, 4_7_kΩ.Pin_1, R1.Pin_1
